# Fritzing sketch HUMAN_FOLLOWING_ROBOT (saved by Fritzing 0.9.5d)
# 18650 Li-ion Battery: CC-BY Dr Kristofer Chan, King's College London/Remote-research.org
breadboards: 1

parts:
  L298N1 = L298N DC motor driver
  M1 = Getriebemotor
  M2 = Getriebemotor
  BAT1 = 18650 Li-ion Battery [package=battery-18650]
  BAT2 = 18650 Li-ion Battery [package=battery-18650]
  SW1 = Slide_Switch_new
  HC-SR04_Sensor_1 = HC-SR04 Ultrasonic Distance Sensor
  HC-SR04_Sensor_2 = HC-SR04 Ultrasonic Distance Sensor
  Part1 = Arduino Uno (Rev3)

nets:
  N1: L298N1.OUT1, M2.pin_1
  N2: L298N1.OUT2, M2.pin_2
  N3: L298N1.OUT3, M1.pin_1
  N4: L298N1.12V, BAT2.+
  GND: L298N1.GND, BAT1.-, HC-SR04_Sensor_1.GND, HC-SR04_Sensor_2.GND, Part1.GND
  VCC: L298N1.5V, HC-SR04_Sensor_1.VCC, HC-SR04_Sensor_2.VCC, Part1.VIN
  N5: L298N1.ENA, Part1.D5_PWM
  N6: L298N1.ENB, Part1.D6_PWM
  N7: L298N1.IN2, Part1.D10_PWM/SS
  N8: L298N1.IN3, Part1.D2
  N9: BAT1.+, SW1.pin_2
  N10: BAT2.-, SW1.pin_1
  N11: HC-SR04_Sensor_1.TRIG, Part1.D13/SCK
  N12: HC-SR04_Sensor_1.ECHO, Part1.D12/MISO
  N13: HC-SR04_Sensor_2.TRIG, Part1.D8
  N14: HC-SR04_Sensor_2.ECHO, Part1.D9_PWM

custom parts:
  L298N DC motor driver: 2x DC motor driver with 78M05 positive voltage regulator (7..35 V) L298N: max 46 V, 2 A Set 5 V Enable jumper to enable 5 V regultor (needed for the L298N) and +5 V output at screw terminal or supply external +5 V at screw terminal Set ENA and/or ENB to +5 V to enable motor permanently or supply ENA and/or ENB with PWM signal IN1 and IN2 set rotation directory for motor A (OUT1/OUT2) IN2 and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
  18650 Li-ion Battery: 18650 li-ion Battery Standard 18650 battery with interactive connectors Creative Common Attribution 4.0 International (CC-BY 4.0) license. Any use of this part requires attribution of Dr Kristofer Chan, Department of Geography, King's College London. Contact kristofer.chan [at] kcl.ac.uk OR kris [at] remote-research.org for further information.
  Slide_Switch_new: the New two pin slide switch
